// Logisim project FinalProject.circ as structural Verilog: 1 circuit, main circuit main
module main (
  input  Reset_RAM,
  input  Manual_cycle,
  input  Reset
);

  wire alu_1_p5, Goto_enable, main_2_ram_read, main_2_ram_write, main_2_register_write;
  wire [1:0] main_1_state;
  wire [3:0] A, alu_1_p4, B, D, decoder_1_goto_imm, decoder_1_opcode, imm1, imm2;
  wire [7:0] bit_extender_1_out, controlled_buffer_1_out, Instruction_num;
  wire [15:0] rom_1_data;
  wire [31:0] alu_1_p6, n16_register_file_1_a, n16_register_file_1_b;

  Decoder decoder_1 (
    .Input(rom_1_data), .Destination_register(D), .opcode(decoder_1_opcode), .RegB(B), .RegA(A), .Imm1(imm1),
    .Imm2(imm2), .GoTo_Imm(decoder_1_goto_imm));
  assign bit_extender_1_out = {{4{1'b0}}, decoder_1_goto_imm};  // Bit_Extender bit_extender_1
  ROM #(.dataWidth(16)) rom_1 (.data(rom_1_data));  // open: addr, sel
  assign controlled_buffer_1_out = Goto_enable ? bit_extender_1_out : 8'bz;  // Controlled_Buffer controlled_buffer_1
  _16_register_file u_16_register_file_1 (
    .d(alu_1_p6), .Clk(main_2_register_write), .Rd(D), .Ra(A), .Rb(B), .a(n16_register_file_1_a),
    .b(n16_register_file_1_b));  // open: Clr
  Clock_main main_1 (
    .Increment_by(controlled_buffer_1_out), .Manual_Cycle(Manual_cycle), .Reset(Reset),
    .Counter(Instruction_num), .State(main_1_state));
  // ALU alu_1: pin names not known; wires that end beside it: n16_register_file_1_a, n16_register_file_1_b, imm1, alu_1_p4, alu_1_p5, alu_1_p6
  cliff_bus_control_11_07_15_main main_2 (
    .Cycle_LSB(main_1_state[0]), .Cycle_MSB(main_1_state[1]), .OP(decoder_1_opcode), .ALU_Enable(alu_1_p5),
    .Register_Write(main_2_register_write), .RAM_Read(main_2_ram_read), .RAM_Write(main_2_ram_write),
    .OPCode_to_ALU(alu_1_p4), .Program_Counter_Update(Goto_enable));
  RAM #(.dataWidth(32), .bus("separate")) ram_1 (
    .data(alu_1_p6), .str(main_2_ram_write), .ld(main_2_ram_read), .clr(Reset_RAM));  // open: addr, din, sel, clk

  // Notes on the sheet:
  //   ROM (Instructions)
  //   Clock
  //   Registers
  //   32-bit CPU
  //   By Cliff, Will, Tom, & Crissy
  //   ALU
  //   Bus Control
  //   RAM
endmodule
